// Logisim project LOTP_8-Bit-CPU-V4.circ as structural Verilog: 2 circuits, main circuit main
module main (
  input  in_1
);

  wire CLK, clock_1_out, counter_1_carry, Counter_Up, HALT, nor_1_out, nor_2_out, nor_3_out, not_1_out,
       or_1_out, Overflow, R_ALU, R_AREG, R_Counter, R_INPUT, R_IREG, R_PrgEEPROM, R_STKMEM, Reset_Microcode,
       RST, StackDown, StackUp, undriven_2, W_ADR_REG, W_AREG, W_BREG, W_CALREG, W_Counter, W_IREG, W_OUT,
       W_PrgEEPROM, W_STKMEM, Zero;
  wire [3:0] controlled_buffer_1_out, controlled_buffer_1_out_2, counter_1_q, register_3_q;
  wire [7:0] controlled_buffer_7_out, counter_2_q, counter_3_q, ram_1_data, register_1_q, register_2_q,
       register_4_q, register_5_q, register_6_q, register_7_q, rom_1_data, undriven;
  wire [7:5] rom_2_data;

  assign {controlled_buffer_1_out_2, controlled_buffer_1_out} = R_IREG ? register_2_q : 8'bz;  // Controlled_Buffer controlled_buffer_1
  Pull_Resistor pull_resistor_1 (.node(Overflow));
  Pull_Resistor pull_resistor_2 (.node(Zero));
  Counter #(.width(4), .max('hf)) counter_1 (
    .load(Reset_Microcode), .D(4'b0000), .count(not_1_out), .Q(counter_1_q), .carry(counter_1_carry),
    .clk(CLK), .clr(RST));
  not not_1 (not_1_out, Reset_Microcode);
  Register register_1 (
    .D({controlled_buffer_1_out_2, controlled_buffer_1_out}), .en(W_ADR_REG), .Q(register_1_q), .clk(CLK),
    .clr(RST));
  Register register_2 (
    .D({controlled_buffer_1_out_2, controlled_buffer_1_out}), .en(W_IREG), .Q(register_2_q), .clk(CLK),
    .clr(RST));
  Decoder #(.select(4), .disabled(0), .enable("false")) decoder_1 (
    .out1(R_Counter), .out2(R_PrgEEPROM), .out3(R_IREG), .out4(R_AREG), .out5(R_INPUT), .out6(R_STKMEM),
    .out7(R_ALU), .sel(rom_1_data[3:0]));  // open: out0, out8, out9, out10, out11, out12, out13, out14, out15
  ROM #(.addrWidth(10)) rom_1 (
    .addr({Zero, Overflow, register_2_q[3:0], counter_1_q}), .data(rom_1_data));  // open: sel
  ROM #(.addrWidth(10)) rom_2 (
    .addr({Zero, Overflow, register_2_q[3:0], counter_1_q}),
    .data({rom_2_data, Reset_Microcode, StackDown, StackUp, Counter_Up, HALT}));  // open: sel
  or or_1 (or_1_out, Counter_Up, counter_1_carry);
  Counter counter_2 (
    .load(W_Counter), .D({controlled_buffer_1_out_2, controlled_buffer_1_out}), .count(or_1_out),
    .Q(counter_2_q), .clk(CLK), .clr(RST));  // open: carry
  RAM ram_1 (.addr(register_1_q), .data(ram_1_data), .clk(CLK), .ld(R_PrgEEPROM));  // open: sel, clr
  assign {controlled_buffer_1_out_2, controlled_buffer_1_out} = R_Counter ? counter_2_q : 8'bz;  // Controlled_Buffer controlled_buffer_2
  assign ram_1_data = W_PrgEEPROM ? {controlled_buffer_1_out_2, controlled_buffer_1_out} : 8'bz;  // Controlled_Buffer controlled_buffer_3
  assign {controlled_buffer_1_out_2, controlled_buffer_1_out} = R_PrgEEPROM ? ram_1_data : 8'bz;  // Controlled_Buffer controlled_buffer_4
  Decoder #(.select(4), .disabled(0), .enable("false")) decoder_2 (
    .out1(W_Counter), .out2(W_ADR_REG), .out3(W_PrgEEPROM), .out4(W_IREG), .out5(W_AREG), .out6(W_BREG),
    .out7(W_CALREG), .out8(W_OUT), .out9(W_STKMEM), .sel(rom_1_data[7:4]));  // open: out0, out10, out11, out12, out13, out14, out15
  assign {controlled_buffer_1_out_2, controlled_buffer_1_out} = R_INPUT ? register_5_q : 8'bz;  // Controlled_Buffer controlled_buffer_5
  assign {controlled_buffer_1_out_2, controlled_buffer_1_out} = R_AREG ? register_6_q : 8'bz;  // Controlled_Buffer controlled_buffer_6
  Register #(.width(4)) register_3 (
    .D(controlled_buffer_1_out_2), .en(W_CALREG), .Q(register_3_q), .clk(CLK), .clr(RST));
  nor nor_1 (nor_1_out, StackUp, StackDown);
  Counter counter_3 (.load(nor_1_out), .count(StackUp), .Q(counter_3_q), .clk(CLK), .clr(RST));  // open: D, carry
  Register register_4 (
    .D({controlled_buffer_1_out_2, controlled_buffer_1_out}), .en(W_OUT), .Q(register_4_q), .clk(CLK),
    .clr(RST));
  Register register_5 (.D(undriven), .en(undriven_2), .Q(register_5_q), .clk(CLK), .clr(RST));
  Register register_6 (
    .D({controlled_buffer_1_out_2, controlled_buffer_1_out}), .en(W_AREG), .Q(register_6_q), .clk(CLK),
    .clr(RST));
  ALU alu_1 (
    .CAL(register_3_q), .A(register_6_q), .B(register_7_q), .R_ALU(R_ALU),
    .C({controlled_buffer_1_out_2, controlled_buffer_1_out}), .Overflow(Overflow), .Zero(Zero));
  Register register_7 (
    .D({controlled_buffer_1_out_2, controlled_buffer_1_out}), .en(W_BREG), .Q(register_7_q), .clk(CLK),
    .clr(RST));
  assign controlled_buffer_7_out = W_STKMEM ? {controlled_buffer_1_out_2, controlled_buffer_1_out} : 8'bz;  // Controlled_Buffer controlled_buffer_7
  RAM ram_2 (.addr(counter_3_q), .data(controlled_buffer_7_out), .clk(CLK), .ld(R_STKMEM));  // open: sel, clr
  assign {controlled_buffer_1_out_2, controlled_buffer_1_out} = R_STKMEM ? controlled_buffer_7_out : 8'bz;  // Controlled_Buffer controlled_buffer_8
  nor nor_2 (nor_2_out, nor_3_out, in_1);
  Button button_1 (.out(RST));
  Clock clock_1 (.out(clock_1_out));
  and and_1 (CLK, clock_1_out, nor_3_out);
  nor nor_3 (nor_3_out, HALT, nor_2_out);

  // Notes on the sheet:
  //   Register
  //   Microcode EEPROM B
  //   Microcode EEPROM A
  //   Read 
  //   Write
  //   Calculation 
  //   Register
  //   B Register
  //   A Register
  //   OUTPUT
  //   INPUT
endmodule

module ALU (
  input  R_ALU,
  input  [3:0] CAL,
  input  [7:0] A,
  input  [7:0] B,
  output [7:0] C,
  output Overflow,
  output Zero
);

  wire [7:0] xor_1_out;

  // XOR_Gate xor_1 has open pins: out=xor_1_out
  Adder adder_1 (.a(xor_1_out));  // open: b, out, cin, cout
  // OR_Gate or_1 is placed but not wired
  // AND_Gate and_1 is placed but not wired
  // XOR_Gate xor_2 is placed but not wired
  Multiplexer #(.select(3), .width(8)) multiplexer_1 ();  // open: in0, in1, in2, in3, in4, in5, in6, in7, out, sel, en
  Controlled_Buffer #(.width(8)) controlled_buffer_1 (.out(C), .en(R_ALU));  // open: in
endmodule
